// Logisim project KLIMENKO_HW3.circ as structural Verilog: 13 circuits, main circuit main
module main (
);

  wire alu_1_out_4, and_1_out, clock_1_out, control_1_out_2, control_1_out_3, control_1_out_4,
       control_1_out_6, control_1_out_7, control_1_out_8, control_1_out_9, ex_mem_1_out_12, ex_mem_1_out_13,
       ex_mem_1_out_14, ex_mem_1_out_15, ex_mem_1_out_16, ex_mem_1_out_18, id_ex_1_alu_src, id_ex_1_out_17,
       id_ex_1_out_18, id_ex_1_out_19, id_ex_1_out_20, id_ex_1_out_21, id_ex_1_reg_dst, mem_wb_1_out_7,
       mem_wb_1_out_8, not_1_out, not_2_out;
  wire [1:0] control_1_out_5, forwardingunit_1_forward_a, forwardingunit_1_forward_b, id_ex_1_out_23;
  wire [3:0] alucontrol_1_out_3;
  wire [4:0] ex_mem_1_out_21, id_ex_1_instr_15_11, id_ex_1_instr_20_16, id_ex_1_out_28,
       instructionsplitter_1_out15_11, instructionsplitter_1_out20_16, instructionsplitter_1_out25_21,
       mem_wb_1_out_11, multiplexer_5_out;
  wire [5:0] instructionsplitter_1_out31_26;
  wire [15:0] instructionsplitter_1_out15_0;
  wire [31:0] adder_1_out, adder_2_out, alu_1_out_5, bit_extender_1_out, datamemory_1_out_6, ex_mem_1_out_17,
       ex_mem_1_out_19, ex_mem_1_out_20, id_ex_1_out_25, id_ex_1_out_26, id_ex_1_out_27, id_ex_1_out_29,
       if_id_1_out_4, if_id_1_out_5, mem_wb_1_out_9, mem_wb_1_out_10, multiplexer_1_out, multiplexer_2_out,
       multiplexer_3_out, multiplexer_4_out, multiplexer_6_out, register_1_q, registers_1_out_7,
       registers_1_out_8, rom_1_data, shifter_1_out;

  Multiplexer #(.width(32)) multiplexer_1 (
    .in0(adder_1_out), .in1(ex_mem_1_out_17), .out(multiplexer_1_out), .sel(and_1_out));  // open: en
  Register #(.width(32)) register_1 (.D(multiplexer_1_out), .Q(register_1_q), .clk(clock_1_out));  // open: en, clr
  Clock clock_1 (.out(clock_1_out));
  not not_1 (not_1_out, clock_1_out);
  IF_ID if_id_1 (
    .in_2(adder_1_out), .in_3(rom_1_data), .out_4(if_id_1_out_4), .out_5(if_id_1_out_5), .clock(clock_1_out));
  Adder #(.width(32)) adder_1 (.a(register_1_q), .b(32'h4), .out(adder_1_out));  // open: cin, cout
  ROM #(.addrWidth(6), .dataWidth(32)) rom_1 (.addr(register_1_q[7:2]), .data(rom_1_data));  // open: sel
  InstructionSplitter instructionsplitter_1 (
    .instr_in(if_id_1_out_5), .out15_0(instructionsplitter_1_out15_0),
    .out15_11(instructionsplitter_1_out15_11), .out20_16(instructionsplitter_1_out20_16),
    .out25_21(instructionsplitter_1_out25_21), .out31_26(instructionsplitter_1_out31_26));  // open: out5_0
  Control control_1 (
    .in_1(instructionsplitter_1_out31_26), .out_2(control_1_out_2), .out_3(control_1_out_3),
    .out_4(control_1_out_4), .out_6(control_1_out_6), .out_5(control_1_out_5), .out_7(control_1_out_7),
    .out_8(control_1_out_8), .out_9(control_1_out_9));
  Registers registers_1 (
    .in_3(instructionsplitter_1_out25_21), .in_4(instructionsplitter_1_out20_16), .in_5(multiplexer_6_out),
    .in_6(mem_wb_1_out_11), .out_7(registers_1_out_7), .out_8(registers_1_out_8), .in_2(mem_wb_1_out_7),
    .in_1(not_1_out));
  assign bit_extender_1_out = {{16{instructionsplitter_1_out15_0[15]}}, instructionsplitter_1_out15_0};  // Bit_Extender bit_extender_1
  ID_EX id_ex_1 (
    .clock(clock_1_out), .REG_WRITE(control_1_out_2), .in_10(if_id_1_out_4), .in_11(registers_1_out_7),
    .in_12(registers_1_out_8), .in_14(bit_extender_1_out), .in_15(instructionsplitter_1_out20_16),
    .in_16(instructionsplitter_1_out15_11), .out_17(id_ex_1_out_17), .out_25(id_ex_1_out_25),
    .out_26(id_ex_1_out_26), .out_27(id_ex_1_out_27), .out_29(id_ex_1_out_29),
    .instr_20_16(id_ex_1_instr_20_16), .instr_15_11(id_ex_1_instr_15_11), .in_3(control_1_out_6),
    .out_18(id_ex_1_out_18), .BRANCH(control_1_out_8), .out_19(id_ex_1_out_19), .MEM_READ(control_1_out_7),
    .out_20(id_ex_1_out_20), .MEM_WRITE(control_1_out_4), .out_21(id_ex_1_out_21), .in_7(control_1_out_9),
    .REG_DST(id_ex_1_reg_dst), .in_8(control_1_out_5), .out_23(id_ex_1_out_23), .in_9(control_1_out_3),
    .ALU_SRC(id_ex_1_alu_src), .instr_25_21(instructionsplitter_1_out25_21), .out_28(id_ex_1_out_28));
  Multiplexer #(.select(2), .width(32)) multiplexer_2 (
    .in0(id_ex_1_out_26), .in1(multiplexer_6_out), .in2(ex_mem_1_out_19), .out(multiplexer_2_out),
    .sel(forwardingunit_1_forward_a));  // open: in3, en
  Multiplexer #(.select(2), .width(32)) multiplexer_3 (
    .in0(id_ex_1_out_27), .in1(multiplexer_6_out), .in2(ex_mem_1_out_19), .out(multiplexer_3_out),
    .sel(forwardingunit_1_forward_b));  // open: in3, en
  Multiplexer #(.width(32)) multiplexer_4 (
    .in0(multiplexer_3_out), .in1(id_ex_1_out_29), .out(multiplexer_4_out), .sel(id_ex_1_alu_src));  // open: en
  Multiplexer #(.width(5)) multiplexer_5 (
    .in0(id_ex_1_instr_20_16), .in1(id_ex_1_instr_15_11), .out(multiplexer_5_out), .sel(id_ex_1_reg_dst));  // open: en
  ForwardingUnit forwardingunit_1 (
    .in_1(ex_mem_1_out_21), .in_2(mem_wb_1_out_11), .in_3(id_ex_1_out_28), .in_4(id_ex_1_instr_20_16),
    .Forward_A(forwardingunit_1_forward_a), .Forward_B(forwardingunit_1_forward_b),
    .EX_MEM_RegWrite(ex_mem_1_out_12), .MEM_WB_RegWrite(mem_wb_1_out_7));
  Adder #(.width(32)) adder_2 (.a(id_ex_1_out_25), .b(shifter_1_out), .out(adder_2_out));  // open: cin, cout
  Shifter #(.width(32)) shifter_1 (.in(id_ex_1_out_29), .\dist (5'b00010), .out(shifter_1_out));
  ALU alu_1 (
    .in_1(multiplexer_2_out), .in_2(multiplexer_4_out), .out_5(alu_1_out_5), .out_4(alu_1_out_4),
    .in_3(alucontrol_1_out_3));
  ALUControl alucontrol_1 (.ALUOp(id_ex_1_out_23), .in_2(id_ex_1_out_29[5:0]), .out_3(alucontrol_1_out_3));
  EX_MEM ex_mem_1 (
    .clock(clock_1_out), .REG_WRITE(id_ex_1_out_17), .in_3(id_ex_1_out_18), .BRANCH(id_ex_1_out_19),
    .MEM_READ(id_ex_1_out_20), .MEM_WRITE(id_ex_1_out_21), .in_7(adder_2_out), .in_8(alu_1_out_4),
    .in_9(alu_1_out_5), .in_10(multiplexer_3_out), .in_11(multiplexer_5_out), .out_12(ex_mem_1_out_12),
    .out_13(ex_mem_1_out_13), .out_14(ex_mem_1_out_14), .out_15(ex_mem_1_out_15), .out_16(ex_mem_1_out_16),
    .out_17(ex_mem_1_out_17), .out_18(ex_mem_1_out_18), .out_19(ex_mem_1_out_19), .out_20(ex_mem_1_out_20),
    .out_21(ex_mem_1_out_21));
  and and_1 (and_1_out, ex_mem_1_out_14, ex_mem_1_out_18);
  DataMemory datamemory_1 (
    .clock(not_1_out), .in_3(ex_mem_1_out_19), .in_4(ex_mem_1_out_20), .out_6(datamemory_1_out_6),
    .MemWrite(ex_mem_1_out_16), .in_5(ex_mem_1_out_15));
  MEM_WB mem_wb_1 (
    .clock(clock_1_out), .REG_WRITE(ex_mem_1_out_12), .in_3(ex_mem_1_out_13), .in_4(datamemory_1_out_6),
    .in_5(ex_mem_1_out_19), .in_6(ex_mem_1_out_21), .out_7(mem_wb_1_out_7), .out_8(mem_wb_1_out_8),
    .out_9(mem_wb_1_out_9), .out_10(mem_wb_1_out_10), .out_11(mem_wb_1_out_11));
  not not_2 (not_2_out, mem_wb_1_out_8);
  Multiplexer #(.width(32)) multiplexer_6 (
    .in0(mem_wb_1_out_9), .in1(mem_wb_1_out_10), .out(multiplexer_6_out), .sel(not_2_out));  // open: en

  // Notes on the sheet:
  //   PC
  //   Program Memory
  //   contents of rom_1 (hex, n*v repeats v):
  //   8c280000 8c290004 8c2a0008 1605824 1685820 10b5820 16b5820 16a5820 16a5820 16a5820 1695820 ac2b000c
  //   rs
  //   rt
  //   rd
  //   rs
  //   rt
  //   rd
  //   Data
  //   Memory
endmodule

module ALU (
  input  [31:0] in_1,
  input  [31:0] in_2,
  input  [3:0] in_3,
  output out_4,
  output [31:0] out_5
);

  wire [31:0] adder_1_out, and_1_out, bit_extender_1_out, or_1_out, subtractor_1_out;

  assign bit_extender_1_out = {{31{1'b0}}, subtractor_1_out[31]};  // Bit_Extender bit_extender_1
  Adder #(.width(32)) adder_1 (.a(in_1), .b(in_2), .out(adder_1_out));  // open: cin, cout
  Subtractor #(.width(32)) subtractor_1 (.a(in_1), .b(in_2), .out(subtractor_1_out));  // open: bin, bout
  assign and_1_out = in_1 & in_2;  // AND_Gate and_1, 32 bits wide
  assign or_1_out = in_1 | in_2;  // OR_Gate or_1, 32 bits wide
  Multiplexer #(.select(4), .width(32)) multiplexer_1 (
    .in0(and_1_out), .in1(or_1_out), .in2(adder_1_out), .in6(subtractor_1_out), .in7(bit_extender_1_out),
    .out(out_5), .sel(in_3));  // open: in3, in4, in5, in8, in9, in10, in11, in12, in13, in14, in15, en
  Comparator #(.width(32)) comparator_1 (.a({32{1'b0}}), .b(out_5), .eq(out_4));  // open: gt, lt
endmodule

module Registers (
  input  in_1,
  input  in_2,
  input  [4:0] in_3,
  input  [4:0] in_4,
  input  [31:0] in_5,
  input  [4:0] in_6,
  output [31:0] out_7,
  output [31:0] out_8
);

  wire demultiplexer_1_out0, demultiplexer_1_out1, demultiplexer_1_out2, demultiplexer_1_out3;
  wire [31:0] reg8_1_out_7, reg8_1_out_8, reg8_2_out_7, reg8_2_out_8, reg8_3_out_7, reg8_3_out_8,
       reg8_4_out_7, reg8_4_out_8;

  Demultiplexer #(.select(2)) demultiplexer_1 (
    .out0(demultiplexer_1_out0), .out1(demultiplexer_1_out1), .out2(demultiplexer_1_out2),
    .out3(demultiplexer_1_out3), .in(in_2), .sel(in_6[4:3]));  // open: en
  Reg8 reg8_1 (
    .in_4(in_4[2:0]), .in_5(in_5), .in_6(in_6[2:0]), .out_7(reg8_1_out_7), .out_8(reg8_1_out_8),
    .in_2(demultiplexer_1_out0), .in_1(in_1), .in_3(in_3[2:0]));
  Reg8 reg8_2 (
    .in_4(in_4[2:0]), .in_5(in_5), .in_6(in_6[2:0]), .out_7(reg8_2_out_7), .out_8(reg8_2_out_8),
    .in_2(demultiplexer_1_out1), .in_1(in_1), .in_3(in_3[2:0]));
  Reg8 reg8_3 (
    .in_4(in_4[2:0]), .in_5(in_5), .in_6(in_6[2:0]), .out_7(reg8_3_out_7), .out_8(reg8_3_out_8),
    .in_2(demultiplexer_1_out2), .in_1(in_1), .in_3(in_3[2:0]));
  Reg8 reg8_4 (
    .in_4(in_4[2:0]), .in_5(in_5), .in_6(in_6[2:0]), .out_7(reg8_4_out_7), .out_8(reg8_4_out_8),
    .in_2(demultiplexer_1_out3), .in_1(in_1), .in_3(in_3[2:0]));
  Multiplexer #(.select(2), .width(32)) multiplexer_1 (
    .in0(reg8_1_out_7), .in1(reg8_2_out_7), .in2(reg8_3_out_7), .in3(reg8_4_out_7), .out(out_7),
    .sel(in_3[4:3]));  // open: en
  Multiplexer #(.select(2), .width(32)) multiplexer_2 (
    .in0(reg8_1_out_8), .in1(reg8_2_out_8), .in2(reg8_3_out_8), .in3(reg8_4_out_8), .out(out_8),
    .sel(in_4[4:3]));  // open: en
endmodule

module Reg8 (
  input  in_1,
  input  in_2,
  input  [2:0] in_3,
  input  [2:0] in_4,
  input  [31:0] in_5,
  input  [2:0] in_6,
  output [31:0] out_7,
  output [31:0] out_8
);

  wire demultiplexer_1_out0, demultiplexer_1_out1, demultiplexer_1_out2, demultiplexer_1_out3,
       demultiplexer_1_out4, demultiplexer_1_out5, demultiplexer_1_out6, demultiplexer_1_out7;
  wire [31:0] register_1_q, register_2_q, register_3_q, register_4_q, register_5_q, register_6_q,
       register_7_q, register_8_q;

  Demultiplexer #(.select(3)) demultiplexer_1 (
    .out0(demultiplexer_1_out0), .out1(demultiplexer_1_out1), .out2(demultiplexer_1_out2),
    .out3(demultiplexer_1_out3), .out4(demultiplexer_1_out4), .out5(demultiplexer_1_out5),
    .out6(demultiplexer_1_out6), .out7(demultiplexer_1_out7), .in(in_2), .sel(in_6));  // open: en
  Register #(.width(32)) register_1 (.D(in_5), .en(demultiplexer_1_out0), .Q(register_1_q), .clk(in_1));  // open: clr
  Register #(.width(32)) register_2 (.D(in_5), .en(demultiplexer_1_out1), .Q(register_2_q), .clk(in_1));  // open: clr
  Register #(.width(32)) register_3 (.D(in_5), .en(demultiplexer_1_out2), .Q(register_3_q), .clk(in_1));  // open: clr
  Register #(.width(32)) register_4 (.D(in_5), .en(demultiplexer_1_out3), .Q(register_4_q), .clk(in_1));  // open: clr
  Register #(.width(32)) register_5 (.D(in_5), .en(demultiplexer_1_out4), .Q(register_5_q), .clk(in_1));  // open: clr
  Register #(.width(32)) register_6 (.D(in_5), .en(demultiplexer_1_out5), .Q(register_6_q), .clk(in_1));  // open: clr
  Register #(.width(32)) register_7 (.D(in_5), .en(demultiplexer_1_out6), .Q(register_7_q), .clk(in_1));  // open: clr
  Register #(.width(32)) register_8 (.D(in_5), .en(demultiplexer_1_out7), .Q(register_8_q), .clk(in_1));  // open: clr
  Multiplexer #(.select(3), .width(32)) multiplexer_1 (
    .in0(register_1_q), .in1(register_2_q), .in2(register_3_q), .in3(register_4_q), .in4(register_5_q),
    .in5(register_6_q), .in6(register_7_q), .in7(register_8_q), .out(out_7), .sel(in_3));  // open: en
  Multiplexer #(.select(3), .width(32)) multiplexer_2 (
    .in0(register_1_q), .in1(register_2_q), .in2(register_3_q), .in3(register_4_q), .in4(register_5_q),
    .in5(register_6_q), .in6(register_7_q), .in7(register_8_q), .out(out_8), .sel(in_4));  // open: en
endmodule

module DataMemory (
  input  MemWrite,
  input  clock,
  input  [31:0] in_3,
  input  [31:0] in_4,
  input  in_5,
  output [31:0] out_6
);

  RAM #(.addrWidth(6), .dataWidth(32), .bus("separate")) ram_1 (
    .addr(in_3[7:2]), .din(in_4), .data(out_6), .str(MemWrite), .sel(1'b1), .clk(clock), .ld(in_5));  // open: clr

  // Notes on the sheet:
  //   address
  //   in data
  //   MemRead
  //   out data
endmodule

module Control (
  input  [5:0] in_1,
  output out_2,
  output out_3,
  output out_4,
  output [1:0] out_5,
  output out_6,
  output out_7,
  output out_8,
  output out_9
);

  ROM #(.addrWidth(6), .dataWidth(9)) rom_1 (
    .addr(in_1), .data({out_9, out_8, out_7, out_6, out_5, out_4, out_3, out_2}));  // open: sel

  // Notes on the sheet:
  //   contents of rom_1 (hex, n*v repeats v):
  //   111 0 0 0 88 30*0 63 7*0 6
endmodule

module ALUControl (
  input  [1:0] ALUOp,
  input  [5:0] in_2,
  output [3:0] out_3
);

  wire [3:0] multiplexer_1_out;

  Multiplexer #(.select(4), .width(4)) multiplexer_1 (
    .in0(4'b0010), .in2(4'b0110), .in4(4'b0000), .in5(4'b0001), .in10(4'b0111), .out(multiplexer_1_out),
    .sel(in_2[3:0]));  // open: in1, in3, in6, in7, in8, in9, in11, in12, in13, in14, in15, en
  Multiplexer #(.select(2), .width(4)) multiplexer_2 (
    .in0(4'b0010), .in1(4'b0110), .in2(multiplexer_1_out), .out(out_3), .sel(ALUOp));  // open: in3, en

  // Notes on the sheet:
  //   Func Field
endmodule

module InstructionSplitter (
  input  [31:0] instr_in,
  output [5:0] out5_0,
  output [15:0] out15_0,
  output [4:0] out15_11,
  output [4:0] out20_16,
  output [4:0] out25_21,
  output [5:0] out31_26
);


  assign out5_0 = instr_in[5:0];
  assign out15_0 = instr_in[15:0];
  assign out15_11 = instr_in[15:11];
  assign out20_16 = instr_in[20:16];
  assign out25_21 = instr_in[25:21];
  assign out31_26 = instr_in[31:26];
endmodule

module IF_ID (
  input  clock,
  input  [31:0] in_2,
  input  [31:0] in_3,
  output [31:0] out_4,
  output [31:0] out_5
);

  Register #(.width(32)) register_1 (.D(in_2), .Q(out_4), .clk(clock));  // open: en, clr
  Register #(.width(32)) register_2 (.D(in_3), .Q(out_5), .clk(clock));  // open: en, clr

  // Notes on the sheet:
  //   pc + 4
  //   instruction
endmodule

module ID_EX (
  input  clock,
  input  REG_WRITE,
  input  in_3,
  input  BRANCH,
  input  MEM_READ,
  input  MEM_WRITE,
  input  in_7,
  input  [1:0] in_8,
  input  in_9,
  input  [31:0] in_10,
  input  [31:0] in_11,
  input  [31:0] in_12,
  input  [4:0] instr_25_21,
  input  [31:0] in_14,
  input  [4:0] in_15,
  input  [4:0] in_16,
  output out_17,
  output out_18,
  output out_19,
  output out_20,
  output out_21,
  output REG_DST,
  output [1:0] out_23,
  output ALU_SRC,
  output [31:0] out_25,
  output [31:0] out_26,
  output [31:0] out_27,
  output [4:0] out_28,
  output [31:0] out_29,
  output [4:0] instr_20_16,
  output [4:0] instr_15_11
);

  Register #(.width(1)) register_1 (.D(REG_WRITE), .Q(out_17), .clk(clock));  // open: en, clr
  Register #(.width(1)) register_2 (.D(in_3), .Q(out_18), .clk(clock));  // open: en, clr
  Register #(.width(1)) register_3 (.D(BRANCH), .Q(out_19), .clk(clock));  // open: en, clr
  Register #(.width(1)) register_4 (.D(MEM_READ), .Q(out_20), .clk(clock));  // open: en, clr
  Register #(.width(1)) register_5 (.D(MEM_WRITE), .Q(out_21), .clk(clock));  // open: en, clr
  Register #(.width(1)) register_6 (.D(in_7), .Q(REG_DST), .clk(clock));  // open: en, clr
  Register #(.width(2)) register_7 (.D(in_8), .Q(out_23), .clk(clock));  // open: en, clr
  Register #(.width(1)) register_8 (.D(in_9), .Q(ALU_SRC), .clk(clock));  // open: en, clr
  Register #(.width(32)) register_9 (.D(in_10), .Q(out_25), .clk(clock));  // open: en, clr
  Register #(.width(32)) register_10 (.D(in_11), .Q(out_26), .clk(clock));  // open: en, clr
  Register #(.width(32)) register_11 (.D(in_12), .Q(out_27), .clk(clock));  // open: en, clr
  Register #(.width(5)) register_12 (.D(instr_25_21), .Q(out_28), .clk(clock));  // open: en, clr
  Register #(.width(32)) register_13 (.D(in_14), .Q(out_29), .clk(clock));  // open: en, clr
  Register #(.width(5)) register_14 (.D(in_15), .Q(instr_20_16), .clk(clock));  // open: en, clr
  Register #(.width(5)) register_15 (.D(in_16), .Q(instr_15_11), .clk(clock));  // open: en, clr

  // Notes on the sheet:
  //   MEM TO REG
  //   ALU OP
  //   WB
  //   M
  //   EX
  //   pc + 4
  //   read data 1
  //   read data 2
  //   sext
endmodule

module EX_MEM (
  input  clock,
  input  REG_WRITE,
  input  in_3,
  input  BRANCH,
  input  MEM_READ,
  input  MEM_WRITE,
  input  [31:0] in_7,
  input  in_8,
  input  [31:0] in_9,
  input  [31:0] in_10,
  input  [4:0] in_11,
  output out_12,
  output out_13,
  output out_14,
  output out_15,
  output out_16,
  output [31:0] out_17,
  output out_18,
  output [31:0] out_19,
  output [31:0] out_20,
  output [4:0] out_21
);

  Register #(.width(1)) register_1 (.D(REG_WRITE), .Q(out_12), .clk(clock));  // open: en, clr
  Register #(.width(1)) register_2 (.D(in_3), .Q(out_13), .clk(clock));  // open: en, clr
  Register #(.width(1)) register_3 (.D(BRANCH), .Q(out_14), .clk(clock));  // open: en, clr
  Register #(.width(1)) register_4 (.D(MEM_READ), .Q(out_15), .clk(clock));  // open: en, clr
  Register #(.width(1)) register_5 (.D(MEM_WRITE), .Q(out_16), .clk(clock));  // open: en, clr
  Register #(.width(32)) register_6 (.D(in_7), .Q(out_17), .clk(clock));  // open: en, clr
  Register #(.width(1)) register_7 (.D(in_8), .Q(out_18), .clk(clock));  // open: en, clr
  Register #(.width(32)) register_8 (.D(in_9), .Q(out_19), .clk(clock));  // open: en, clr
  Register #(.width(32)) register_9 (.D(in_10), .Q(out_20), .clk(clock));  // open: en, clr
  Register #(.width(5)) register_10 (.D(in_11), .Q(out_21), .clk(clock));  // open: en, clr

  // Notes on the sheet:
  //   MEM TO REG
  //   WB
  //   M
  //   add result
  //   zero
  //   alu result
  //   read data 2
  //   mux res
endmodule

module MEM_WB (
  input  clock,
  input  REG_WRITE,
  input  in_3,
  input  [31:0] in_4,
  input  [31:0] in_5,
  input  [4:0] in_6,
  output out_7,
  output out_8,
  output [31:0] out_9,
  output [31:0] out_10,
  output [4:0] out_11
);

  Register #(.width(1)) register_1 (.D(REG_WRITE), .Q(out_7), .clk(clock));  // open: en, clr
  Register #(.width(1)) register_2 (.D(in_3), .Q(out_8), .clk(clock));  // open: en, clr
  Register #(.width(32)) register_3 (.D(in_4), .Q(out_9), .clk(clock));  // open: en, clr
  Register #(.width(32)) register_4 (.D(in_5), .Q(out_10), .clk(clock));  // open: en, clr
  Register #(.width(5)) register_5 (.D(in_6), .Q(out_11), .clk(clock));  // open: en, clr

  // Notes on the sheet:
  //   MEM TO REG
  //   WB
  //   read data
  //   alu result
  //   mux res
endmodule

module ForwardingUnit (
  input  [4:0] in_1,
  input  [4:0] in_2,
  input  [4:0] in_3,
  input  [4:0] in_4,
  input  EX_MEM_RegWrite,
  input  MEM_WB_RegWrite,
  output [1:0] Forward_A,
  output [1:0] Forward_B
);

  wire and_1_out, and_2_out, and_3_out, and_4_out, comparator_1_eq, comparator_2_eq, comparator_3_eq,
       comparator_4_eq, comparator_5_eq, comparator_6_eq, comparator_7_eq, comparator_8_eq, not_1_out,
       not_2_out, not_3_out, not_4_out, not_5_out, not_6_out;

  Comparator #(.width(5)) comparator_1 (.a(in_1), .b({5{1'b0}}), .eq(comparator_1_eq));  // open: gt, lt
  Comparator #(.width(5)) comparator_2 (.a(in_1), .b(in_3), .eq(comparator_2_eq));  // open: gt, lt
  Comparator #(.width(5)) comparator_3 (.a(in_1), .b({5{1'b0}}), .eq(comparator_3_eq));  // open: gt, lt
  Comparator #(.width(5)) comparator_4 (.a(in_1), .b(in_4), .eq(comparator_4_eq));  // open: gt, lt
  Comparator #(.width(5)) comparator_5 (.a(in_2), .b({5{1'b0}}), .eq(comparator_5_eq));  // open: gt, lt
  Comparator #(.width(5)) comparator_6 (.a(in_2), .b(in_3), .eq(comparator_6_eq));  // open: gt, lt
  Comparator #(.width(5)) comparator_7 (.a(in_2), .b({5{1'b0}}), .eq(comparator_7_eq));  // open: gt, lt
  Comparator #(.width(5)) comparator_8 (.a(in_2), .b(in_4), .eq(comparator_8_eq));  // open: gt, lt
  not not_1 (not_1_out, comparator_1_eq);
  and and_1 (and_1_out, not_1_out, EX_MEM_RegWrite);
  not not_2 (not_2_out, comparator_3_eq);
  and and_2 (and_2_out, not_2_out, EX_MEM_RegWrite);
  not not_3 (not_3_out, comparator_5_eq);
  and and_3 (and_3_out, not_3_out, MEM_WB_RegWrite);
  not not_4 (not_4_out, comparator_7_eq);
  and and_4 (and_4_out, not_4_out, MEM_WB_RegWrite);
  and and_5 (Forward_A[1], and_1_out, comparator_2_eq);
  and and_6 (Forward_B[1], and_2_out, comparator_4_eq);
  not not_5 (not_5_out, Forward_A[1]);
  and and_7 (Forward_A[0], not_5_out, and_3_out, comparator_6_eq);
  not not_6 (not_6_out, Forward_B[1]);
  and and_8 (Forward_B[0], not_6_out, and_4_out, comparator_8_eq);

  // Notes on the sheet:
  //   EX/MEM.RegisterRd
  //   MEM/WB.RegisterRd
  //   ID/EX.RegisterRs
  //   ID/EX.RegisterRt
  //   EX Hazard ForwardA = 10
  //   EX Hazard ForwardB = 10
  //   MEM Hazard ForwardA = 01
  //   MEM Hazard ForwardB = 01
endmodule
